# Fritzing sketch 555_Timer_Circuit_Breadboard (saved by Fritzing 0.9.5d)
breadboards: 1

parts:
  U1 = 555 Timer [package="DIP8 [THT]"]
  R1 = Resistor [tolerance=±5% resistance=2M package="1206 [SMD]"]
  R2 = Resistor [tolerance=±5% resistance=220 package="1206 [SMD]"]
  C1 = Ceramic Capacitor [capacitance=10pF package="0603 [SMD, multilayer]"]
  C2 = Electrolytic Capacitor [capacitance=200µF voltage=16V package="1010 [SMD, electrolytic]"]
  R3 = Resistor [tolerance=±5% resistance=100k package="1206 [SMD]"]
  Q1 = NPN-Transistor [package="SOT-23 [SMD]"]
  R4 = Resistor [tolerance=±5% resistance=100k package="1206 [SMD]"]
  Q2 = NPN-Transistor [package="SOT-23 [SMD]"]
  D1 = Rectifier Diode [part_number=1N4001 package="Melf DO-213 AB [SMD]"]
  U2 = RELAY [package=relay-t9a-2]

nets:
  N1: U1.Ground, C1.1, C2.-, Q1.1, R4.Pin_0, Q2.1, D1.cathode
  N2: U1.Trigger, U1.Threshold, R1.Pin_1, C2.+
  N3: U1.Output, R3.Pin_1
  N4: U1.Reset, U1.Vcc_Supply_Voltage, R2.Pin_0, U2.NC
  N5: U1.Control_Voltage, C1.0
  N6: U1.Discharge, R1.Pin_0, R2.Pin_1
  N7: R3.Pin_0, Q1.0
  N8: Q1.2, R4.Pin_1, Q2.0
  N9: Q2.2, D1.anode, U2.COIL2
