# Fritzing sketch Solar_Battery_Charger_Breadboard (saved by Fritzing 0.9.5d)

parts:
  D1 = SOLAR-IXYS [package=solarbit-12x1]
  18650_Lithium_Battery = Battery Holders [package=battery-aa]
  Part3 = Power Cell LiPo Charger/Booster
  Part2 = USB LiPoly Charger
  D2 = Rectifier Diode [part_number=1N4004 package="300 mil [THT]"]

nets:
  GND: D1.A, 18650_Lithium_Battery.+, Part3.GND, Part2.GND
  N1: D1.C, D2.anode
  N2: 18650_Lithium_Battery.-, Part3.VBATT, Part2.VBAT, D2.cathode
